// Logisim project TallerLogica-Combinatorios.circ as structural Verilog: 8 circuits, main circuit sumador_simple
module sumador_simple (
  input  a,
  input  b,
  output S,
  output Cout
);

  xor xor_1 (S, a, b);
  and and_1 (Cout, a, b);
endmodule

module sumador_completo (
  input  Cin,
  input  A,
  input  B,
  output S,
  output Cout
);

  wire sumador_simple_1_cout, sumador_simple_2_cout, sumador_simple_2_s;

  sumador_simple sumador_simple_1 (.a(Cin), .b(sumador_simple_2_s), .S(S), .Cout(sumador_simple_1_cout));
  sumador_simple sumador_simple_2 (.a(A), .b(B), .S(sumador_simple_2_s), .Cout(sumador_simple_2_cout));
  or or_1 (Cout, sumador_simple_1_cout, sumador_simple_2_cout);
endmodule

module sumador_4 (
  input  Cin,
  input  [3:0] A,
  input  [3:0] B,
  output [3:0] S,
  output Cout
);

  wire sumador_completo_1_cout, sumador_completo_2_cout, sumador_completo_3_cout;

  sumador_completo sumador_completo_1 (.A(A[0]), .B(B[0]), .Cin(Cin), .S(S[0]), .Cout(sumador_completo_1_cout));
  sumador_completo sumador_completo_2 (
    .A(A[1]), .B(B[1]), .Cin(sumador_completo_1_cout), .S(S[1]), .Cout(sumador_completo_2_cout));
  sumador_completo sumador_completo_3 (
    .A(A[2]), .B(B[2]), .Cin(sumador_completo_2_cout), .S(S[2]), .Cout(sumador_completo_3_cout));
  sumador_completo sumador_completo_4 (.A(A[3]), .B(B[3]), .Cin(sumador_completo_3_cout), .S(S[3]), .Cout(Cout));
  Hex_Digit_Display hex_digit_display_1 (.value(S));  // open: dp
endmodule

module comparador_cero (
  input  [3:0] A,
  output Z
);

  wire or_1_out, or_2_out, or_3_out;

  or or_1 (or_1_out, A[0], A[1]);
  or or_2 (or_2_out, A[2], A[3]);
  or or_3 (or_3_out, or_1_out, or_2_out);
  not not_1 (Z, or_3_out);
endmodule

module sumador_flags (
  input  Cin,
  input  [3:0] A,
  input  [3:0] B,
  output [3:0] S,
  output N,
  output Z,
  output V,
  output C
);

  wire and_2_out, and_3_out, and_4_out, and_5_out, not_2_out, not_3_out, not_4_out;

  // NOT_Gate not_1 is placed but not wired
  // AND_Gate and_1 is placed but not wired
  not not_2 (not_2_out, B[3]);
  // OR_Gate or_1 is placed but not wired
  sumador_4 sumador_4_1 (.Cin(Cin), .A(A), .S({N, S[2:0]}), .B(B), .Cout(C));
  not not_3 (not_3_out, A[3]);
  and and_2 (and_2_out, not_3_out, not_2_out);
  and and_3 (and_3_out, N, and_2_out);
  not not_4 (not_4_out, N);
  and and_4 (and_4_out, A[3], B[3]);
  comparador_cero comparador_cero_1 (.A({N, S[2:0]}), .Z(Z));
  or or_2 (V, and_3_out, and_5_out);
  and and_5 (and_5_out, not_4_out, and_4_out);
  Hex_Digit_Display hex_digit_display_1 (.value({N, S[2:0]}));  // open: dp

  assign S[3] = N;
endmodule

module incrementador_4 (
  input  [3:0] A,
  output [3:0] S
);

  sumador_4 sumador_4_1 (.Cin(1'b0), .A(A), .S(S), .B(4'b0001));  // open: Cout
  Hex_Digit_Display hex_digit_display_1 (.value(S));  // open: dp
endmodule

module inversor_4 (
  input  [3:0] A,
  input  INV,
  output [3:0] S
);

  wire not_1_out, not_2_out, not_3_out, not_4_out, not_5_out;
  wire [3:0] and_1_out, and_5_out, incrementador_4_1_s;

  not not_1 (not_1_out, INV);
  and and_1 (and_1_out[0], A[0], not_1_out);
  and and_2 (and_1_out[1], A[1], not_1_out);
  and and_3 (and_1_out[2], A[2], not_1_out);
  and and_4 (and_1_out[3], A[3], not_1_out);
  not not_2 (not_2_out, A[1]);
  not not_3 (not_3_out, A[2]);
  not not_4 (not_4_out, A[3]);
  not not_5 (not_5_out, A[0]);
  and and_5 (and_5_out[0], not_5_out, INV);
  and and_6 (and_5_out[1], not_2_out, INV);
  and and_7 (and_5_out[2], not_3_out, INV);
  and and_8 (and_5_out[3], not_4_out, INV);
  incrementador_4 incrementador_4_1 (.A(and_5_out), .S(incrementador_4_1_s));
  Multiplexer #(.width(4)) multiplexer_1 (.in0(and_1_out), .in1(incrementador_4_1_s), .out(S), .sel(INV));  // open: en
  Hex_Digit_Display hex_digit_display_1 (.value(S));  // open: dp
endmodule

module ALU (
  input  in_1,
  input  [3:0] A,
  input  [3:0] B,
  input  [1:0] OP,
  output N,
  output Z,
  output V,
  output C,
  output [3:0] S
);

  wire AND_3_out, AND_out, not_1_out, SUM_4bit_c;
  wire [3:0] AND_2_out, INV_s, OR_out, SUM_4bit_s;

  inversor_4 INV (.A(B), .INV(OP[0]), .S(INV_s));
  sumador_flags SUM_4bit (.A(A), .B(INV_s), .Cin(in_1), .S(SUM_4bit_s), .V(V), .C(SUM_4bit_c));  // open: N, Z
  and AND (AND_out, SUM_4bit_c, not_1_out);
  not not_1 (not_1_out, OP[0]);
  assign AND_2_out = A & B;  // AND_Gate AND_2, 4 bits wide
  assign OR_out = A | B;  // OR_Gate OR, 4 bits wide
  or OR_2 (C, AND_out, AND_3_out);
  and AND_3 (AND_3_out, SUM_4bit_c, OP[0]);
  comparador_cero CMP_Z (.A({N, S[2:0]}), .Z(Z));
  Hex_Digit_Display hex_digit_display_1 (.value({N, S[2:0]}));  // open: dp
  Multiplexer #(.select(2), .width(4)) multiplexer_1 (
    .in0(SUM_4bit_s), .in1(SUM_4bit_s), .in2(AND_2_out), .in3(OR_out), .out({N, S[2:0]}), .sel(OP));  // open: en

  assign S[3] = N;

  // Other names for the same wires on the sheet: OP1 = OP[0]
endmodule
