// Logisim project micro8reg.circ as structural Verilog: 10 circuits, main circuit DataPath
module DataPath (
  output [15:0] Microinstruccion,
  output [2:0] out_2,
  output [7:0] out_3,
  output HALT
);

  wire clk, clk_out, clock_1_out, decodificador_1_alu, decodificador_1_store, not_1_out, or_1_out, or_2_out,
       reset, reset_counter_out;
  wire [1:0] ALU_OP;
  wire [2:0] decodificador_1_reg_dst, decodificador_1_reg_src;
  wire [3:0] decodificador_1_opcode, flags, Instrucciones_pc, Instrucciones_pc_2;
  wire [4:0] decodificador_1_mem_dir;
  wire [7:0] decodificador_1_mem_data, MicroPC_value_out, next_micro_pc;
  wire [11:0] demultiplexer_1_out1, demultiplexer_1_out2, Instrucciones_instruccion;
  wire [11:1] demultiplexer_1_out3;

  Multiplexer #(.width(8)) multiplexer_1 (
    .in0(next_micro_pc), .in1({8{1'b0}}), .out(out_3), .sel(Microinstruccion[14]));  // open: en
  not not_1 (not_1_out, or_2_out);
  Button button_1 (.out(reset));
  Clock clock_1 (.out(clock_1_out));
  or or_1 (or_1_out, clock_1_out, clk_out);
  Button u_clk (.out(clk_out));
  Counter #(.width(12), .max('hfff)) counter_1 (.clk(clk), .clr(reset_counter_out));  // open: load, D, count, Q, carry
  Button reset_counter (.out(reset_counter_out));
  ROM #(.dataWidth(16)) rom_1 (.addr(MicroPC_value_out), .data(Microinstruccion));  // open: sel
  or or_2 (or_2_out, Microinstruccion[15], Microinstruccion[14]);
  PC MicroPC (
    .value_in(out_3), .inc(not_1_out), .clk(clk), .rst(reset), .load(or_2_out), .value_out(MicroPC_value_out));
  Demultiplexer #(.select(2), .width(12), .disabled(0)) demultiplexer_1 (
    .out1(demultiplexer_1_out1), .out2(demultiplexer_1_out2), .out3({demultiplexer_1_out3, HALT}),
    .in(Microinstruccion[11:0]), .sel(Microinstruccion[13:12]));  // open: out0, en
  and and_1 (clk, ~HALT, or_1_out);  // AND_Gate
  Hex_Digit_Display hex_digit_display_1 (.value(Instrucciones_pc_2));  // open: dp
  Hex_Digit_Display hex_digit_display_2 (.value(Instrucciones_pc));  // open: dp
  Instrucciones Instrucciones (
    .signals(demultiplexer_1_out2), .value_in(decodificador_1_mem_data), .clk(clk), .rst(reset),
    .PC({Instrucciones_pc_2, Instrucciones_pc}), .Flags(flags), .Instruccion(Instrucciones_instruccion));
  Hex_Digit_Display hex_digit_display_3 (.value({1'b0, decodificador_1_reg_dst}));  // open: dp
  Hex_Digit_Display hex_digit_display_4 (.value({1'b0, decodificador_1_reg_src}));  // open: dp
  Hex_Digit_Display hex_digit_display_5 (.value(Instrucciones_instruccion[11:8]));  // open: dp
  Multiplexer #(.width(3)) multiplexer_2 (
    .in0(decodificador_1_reg_src), .in1(decodificador_1_reg_dst), .out(out_2), .sel(decodificador_1_store));  // open: en
  Decodificador decodificador_1 (
    .in_1(Instrucciones_instruccion), .REG_dst(decodificador_1_reg_dst), .REG_src(decodificador_1_reg_src),
    .MEM_dir(decodificador_1_mem_dir), .MEM_data(decodificador_1_mem_data), .Opcode(decodificador_1_opcode),
    .ALU_OP(ALU_OP), .ALU(decodificador_1_alu), .STORE(decodificador_1_store));  // open: MOV, LOAD, MEM, Jxx
  Hex_Digit_Display hex_digit_display_6 (.value(Instrucciones_instruccion[7:4]));  // open: dp
  Hex_Digit_Display hex_digit_display_7 (.value(decodificador_1_mem_data[3:0]));  // open: dp
  Hex_Digit_Display hex_digit_display_8 (.value(decodificador_1_mem_data[7:4]));  // open: dp
  Hex_Digit_Display hex_digit_display_9 (.value(Instrucciones_instruccion[3:0]));  // open: dp
  Data Data (
    .reg_dst_idx(decodificador_1_reg_dst), .reg_src_idx(out_2), .signals(demultiplexer_1_out1),
    .ALU_opcode(ALU_OP), .mem_addr(decodificador_1_mem_dir), .alu_write_op(decodificador_1_alu),
    .Flags(flags), .clk(clk), .reset(reset));
  index_microcode idx_microcode (.SET(decodificador_1_opcode), .addr_idx(next_micro_pc));
  Hex_Digit_Display hex_digit_display_10 (.value(decodificador_1_mem_dir[3:0]));  // open: dp
  Hex_Digit_Display hex_digit_display_11 (.value({3'b000, decodificador_1_mem_dir[4]}));  // open: dp

  // Notes on the sheet:
  //   Contador de clks
  //   contents of rom_1 (hex, n*v repeats v):
  //   0 2002 0 2001 0 8000 0 0 0 1021 0 1091 0 1000 0 1042 0 4000 0 0 0 1009 0 4000 0 0 0 1006 0 4000 0 0
  //   0 1003 0 4000 0 0 0 2004 0 4000 0 0 0 2008 0 4000 0 0 4*ffff 0 0 0 3001 0 0 0 1200 0 1060 0 1091 0
  //   1300 0 1042 0 4000 0 0 0 1200 0 1042 0 4000
  //   PC
  //   REG_dst
  //   REG_src
  //   Instruccion
  //   Mem dir
  //   Data Mem dir
endmodule

// Deco
module Decodificador (
  input  [11:0] in_1,
  output [1:0] ALU_OP,
  output ALU,
  output MOV,
  output LOAD,
  output MEM,
  output STORE,
  output Jxx,
  output [2:0] REG_src,
  output [4:0] MEM_dir,
  output [7:0] MEM_data,
  output [3:0] Opcode,
  output [2:0] REG_dst
);

  wire not_1_out;

  and and_1 (ALU, ~in_1[10], ~in_1[11]);  // AND_Gate
  and and_2 (MOV, in_1[9], in_1[10], ~in_1[11]);  // AND_Gate
  and and_3 (MEM, ~in_1[9], in_1[10], ~in_1[11]);  // AND_Gate
  not not_1 (not_1_out, in_1[8]);
  and and_4 (LOAD, in_1[8], MEM);
  and and_5 (STORE, MEM, not_1_out);

  assign ALU_OP = in_1[9:8];
  assign Jxx = in_1[11];
  assign MEM_data = in_1[7:0];
  assign MEM_dir = in_1[4:0];
  assign Opcode = in_1[11:8];
  assign REG_dst = in_1[7:5];
  assign REG_src = in_1[4:2];

  // Notes on the sheet:
  //   X
endmodule

module Instrucciones (
  input  [11:0] signals,
  input  [3:0] Flags,
  input  [7:0] value_in,
  input  clk,
  input  rst,
  output [7:0] PC,
  output [11:0] Instruccion
);

  wire and_1_out, and_2_out, or_1_out, or_2_out;
  wire [11:0] rom_1_data;

  or or_1 (or_1_out, signals[2], or_2_out);
  PC u_PC (.value_in(value_in), .inc(signals[0]), .clk(clk), .rst(rst), .load(or_1_out), .value_out(PC));
  or or_2 (or_2_out, and_2_out, and_1_out);
  and and_1 (and_1_out, signals[3], Flags[2]);
  and and_2 (and_2_out, signals[4], Flags[3]);
  ROM #(.dataWidth(12)) rom_1 (.addr(PC), .data(rom_1_data));  // open: sel
  Register #(.width(12)) IR (.D(rom_1_data), .en(signals[1]), .Q(Instruccion), .clk(clk), .clr(rst));

  // Notes on the sheet:
  //   X
  //   Memoria de Instrucciones
  //   NZCV
endmodule

module PC (
  input  load,
  input  [7:0] value_in,
  input  inc,
  input  clk,
  input  rst,
  output [7:0] value_out
);

  Counter counter_1 (.load(load), .D(value_in), .count(inc), .Q(value_out), .clk(clk), .clr(rst));  // open: carry
endmodule

module Data (
  input  [1:0] ALU_opcode,
  input  [2:0] reg_dst_idx,
  input  [2:0] reg_src_idx,
  input  [11:0] signals,
  input  alu_write_op,
  input  [4:0] mem_addr,
  input  clk,
  input  reset,
  output [3:0] Flags
);

  wire [2:0] multiplexer_1_out;
  wire [3:0] Registros_data_out, Registros_data_out_2;

  Multiplexer #(.width(3)) multiplexer_1 (
    .in0(reg_src_idx), .in1(reg_dst_idx), .out(multiplexer_1_out), .sel(signals[7]));  // open: en
  _8Reg_bank Registros (
    .data_in({Registros_data_out_2, Registros_data_out}), .w_en(signals[1]), .reg_in_sel(reg_dst_idx),
    .clk(clk), .reset(reset), .reg_out_sel(multiplexer_1_out), .en_out(signals[0]),
    .data_out({Registros_data_out_2, Registros_data_out}));
  Hex_Digit_Display hex_digit_display_1 (.value(Registros_data_out_2));  // open: dp
  Hex_Digit_Display hex_digit_display_2 (.value(Registros_data_out));  // open: dp
  Mem_Data Mem (
    .addr(mem_addr), .data_in({Registros_data_out_2, Registros_data_out}), .load(signals[3]), .clk(clk),
    .reset(reset), .en_out(signals[2]), .data_out({Registros_data_out_2, Registros_data_out}));
  ALU ALU (
    .A({Registros_data_out_2, Registros_data_out}), .A_en(signals[4]),
    .B({Registros_data_out_2, Registros_data_out}), .B_en(signals[5]), .OP(ALU_opcode), .V(Flags[0]),
    .C(Flags[1]), .Z(Flags[2]), .N(Flags[3]), .clk(clk), .reset(reset), .alu_write_op(alu_write_op),
    .en_out(signals[6]), .normalOrCte(signals[9:8]), .ALU_out({Registros_data_out_2, Registros_data_out}));

  // Notes on the sheet:
  //   BUS
  //   X
endmodule

module ALU (
  input  [7:0] A,
  input  A_en,
  input  [1:0] normalOrCte,
  input  [7:0] B,
  input  B_en,
  input  en_out,
  input  [1:0] OP,
  input  clk,
  input  reset,
  input  alu_write_op,
  output Z,
  output N,
  output V,
  output C,
  output [7:0] ALU_out
);

  wire and_2_out, write_op;
  wire [7:0] adder_1_out, and_1_out, multiplexer_1_out, multiplexer_2_out, multiplexer_3_out, not_1_out,
       or_1_out, register_1_q, register_2_q, register_3_q;

  Register register_1 (.D(A), .en(A_en), .Q(register_1_q), .clk(clk), .clr(reset));
  Register register_2 (.D(B), .en(B_en), .Q(register_2_q), .clk(clk), .clr(reset));
  Multiplexer #(.width(8), .enable("false")) multiplexer_1 (
    .in0(register_2_q), .in1(not_1_out), .out(multiplexer_1_out), .sel(OP[0]));
  assign not_1_out = ~register_2_q;  // NOT_Gate not_1, 8 bits wide
  assign and_1_out = register_1_q & register_2_q;  // AND_Gate and_1, 8 bits wide
  assign or_1_out = register_1_q | register_2_q;  // OR_Gate or_1, 8 bits wide
  Adder adder_1 (.a(register_1_q), .b(multiplexer_1_out), .out(adder_1_out), .cin(OP[0]));  // open: cout
  Multiplexer #(.select(2), .width(8), .enable("false")) multiplexer_2 (
    .in0(adder_1_out), .in1(adder_1_out), .in2(and_1_out), .in3(or_1_out), .out(multiplexer_2_out), .sel(OP));
  Multiplexer #(.select(2), .width(8)) multiplexer_3 (
    .in0(multiplexer_2_out), .in1({8{1'b0}}), .in2(8'h1), .in3(multiplexer_2_out), .out(multiplexer_3_out),
    .sel(normalOrCte));  // open: en
  and and_2 (and_2_out, ~multiplexer_2_out[0], ~multiplexer_2_out[1], ~multiplexer_2_out[2], ~multiplexer_2_out[3], ~multiplexer_2_out[4], ~multiplexer_2_out[5], ~multiplexer_2_out[6], ~multiplexer_2_out[7]);  // AND_Gate
  Register register_3 (.D(multiplexer_3_out), .en(write_op), .Q(register_3_q), .clk(clk), .clr(reset));
  assign ALU_out = en_out ? register_3_q : 8'bz;  // Controlled_Buffer controlled_buffer_1
  Register #(.width(1)) register_4 (.D(and_2_out), .en(write_op), .Q(Z), .clk(clk), .clr(reset));
  or or_2 (write_op, normalOrCte[0], normalOrCte[1], alu_write_op);
  Register #(.width(1)) register_5 (.D(multiplexer_2_out[7]), .en(write_op), .Q(N), .clk(clk), .clr(reset));

  // Other names for the same wires on the sheet: sub = OP[0]

  // Notes on the sheet:
  //   X
endmodule

module Mem_Data (
  input  [4:0] addr,
  input  [7:0] data_in,
  input  load,
  input  clk,
  input  reset,
  input  en_out,
  output [7:0] data_out
);

  wire undriven;
  wire [7:0] ram_1_data;

  RAM #(.addrWidth(5), .bus("separate")) ram_1 (
    .addr(addr), .din(data_in), .data(ram_1_data), .str(load), .clk(clk), .clr(undriven));  // open: sel, ld
  assign data_out = en_out ? ram_1_data : 8'bz;  // Controlled_Buffer controlled_buffer_1

  // Notes on the sheet:
  //   X
endmodule

module index_microcode (
  input  [3:0] SET,
  output [7:0] addr_idx
);

  Multiplexer #(.select(4), .width(8)) multiplexer_1 (
    .in0(8'h8), .in1(8'h8), .in2(8'h8), .in3(8'h8), .in4(8'h14), .in5(8'h1a), .in6(8'h38), .in7(8'h20),
    .in8(8'h26), .in9(8'h2c), .in10(8'h32), .in12(8'h3c), .in13(8'h3c), .in14(8'h4a), .out(addr_idx),
    .sel(SET));  // open: in11, in15, en

  // Notes on the sheet:
  //   ALU OP
  //   STORE
  //   LOAD
  //   HALT
  //   MOV
  //   JMP
  //   JE
  //   JN
  //   INC/DEC
  //   X
endmodule

module _4Reg_bank (
  input  [7:0] data_in,
  input  en_out,
  input  w_en,
  input  [1:0] reg_in_sel,
  input  reset,
  input  [1:0] reg_out_sel,
  input  clk,
  output [7:0] data_out
);

  wire decoder_1_out0, decoder_1_out1, decoder_1_out2, decoder_1_out3;
  wire [7:0] multiplexer_1_out, R0_q, R1_q, R2_q, R3_q;

  Decoder #(.select(2), .disabled(0)) decoder_1 (
    .out0(decoder_1_out0), .out1(decoder_1_out1), .out2(decoder_1_out2), .out3(decoder_1_out3),
    .sel(reg_in_sel), .en(w_en));
  Register R0 (.D(data_in), .en(decoder_1_out0), .Q(R0_q), .clk(clk), .clr(reset));
  Register R1 (.D(data_in), .en(decoder_1_out1), .Q(R1_q), .clk(clk), .clr(reset));
  Register R2 (.D(data_in), .en(decoder_1_out2), .Q(R2_q), .clk(clk), .clr(reset));
  Register R3 (.D(data_in), .en(decoder_1_out3), .Q(R3_q), .clk(clk), .clr(reset));
  Multiplexer #(.select(2), .width(8)) multiplexer_1 (
    .in0(R0_q), .in1(R1_q), .in2(R2_q), .in3(R3_q), .out(multiplexer_1_out), .sel(reg_out_sel));  // open: en
  assign data_out = en_out ? multiplexer_1_out : 8'bz;  // Controlled_Buffer controlled_buffer_1

  // Notes on the sheet:
  //   X
endmodule

module _8Reg_bank (
  input  [7:0] data_in,
  input  en_out,
  input  w_en,
  input  [2:0] reg_in_sel,
  input  [2:0] reg_out_sel,
  input  reset,
  input  clk,
  output [7:0] data_out
);

  wire decoder_1_out0, decoder_1_out1;
  wire [7:0] multiplexer_1_out, R0_a_R3_data_out, R4_a_R7_data_out;

  Decoder #(.disabled(0)) decoder_1 (.out0(decoder_1_out0), .out1(decoder_1_out1), .sel(reg_in_sel[2]), .en(w_en));
  _4Reg_bank R0_a_R3 (
    .data_in(data_in), .w_en(decoder_1_out0), .reg_in_sel(reg_in_sel[1:0]), .clk(clk), .reset(reset),
    .reg_out_sel(reg_out_sel[1:0]), .en_out(1'b1), .data_out(R0_a_R3_data_out));
  _4Reg_bank R4_a_R7 (
    .data_in(data_in), .w_en(decoder_1_out1), .reg_in_sel(reg_in_sel[1:0]), .clk(clk), .reset(reset),
    .reg_out_sel(reg_out_sel[1:0]), .en_out(1'b1), .data_out(R4_a_R7_data_out));
  Multiplexer #(.width(8)) multiplexer_1 (
    .in0(R0_a_R3_data_out), .in1(R4_a_R7_data_out), .out(multiplexer_1_out), .sel(reg_out_sel[2]));  // open: en
  assign data_out = en_out ? multiplexer_1_out : 8'bz;  // Controlled_Buffer controlled_buffer_1

  // Notes on the sheet:
  //   X
endmodule
